# Fritzing sketch Untitled Sketch (saved by Fritzing 0.8.7b)

parts:
  元件1 = Arduino Nano (Rev3.0)
  元件2 = SRF05 Ultrasonic Rangefinder
  元件3 = SRF05 Ultrasonic Rangefinder
  S1 = Pushbutton [package="[THT]"]
  S2 = Pushbutton [package="[THT]"]
  S3 = Pushbutton [package="[THT]"]
  DFPlayer_Mini1 = DFPlayer MINI [package="DIP (Dual Inline) [THT]"]
  SP1 = SPEAKER [package=pcb_mount_speaker]
  LED5 = RGB LED (com. cathode, rgb) [package="5 mm [THT]"]
  U1 = LM2596-Step-Down-Converter [package=THT]
  U2 = Mini-USB _B_ connector with 5th pin broken out. [package=usb-minib]
  Mod1 = TP4056 [part_number=TP4056]
  BAT1 = 18650 battery holder [package=battery-18650-kit]
  BAT2 = 18650 battery holder [package=battery-18650-kit]  # not connected
  BAT3 = 18650 battery holder [package=battery-18650-kit]
  U3 = SWITCH_SPDT [package=kps-1290]

nets:
  GND: 元件1.GND, 元件2.GND, 元件3.GND, DFPlayer_Mini1.GND#6, LED5.common_cathode
  N1: 元件1.D2, 元件3.Echo
  N2: 元件1.D3, 元件2.Echo
  N3: 元件1.D4, 元件1.D6, S1.Pin_3, S1.Pin_4, S3.Pin_3, S3.Pin_4
  N4: 元件1.D5, S2.Pin_3, S2.Pin_4
  N5: 元件1.D7, 元件2.Trig, 元件3.Trig
  N6: 元件1.D8, DFPlayer_Mini1.TX
  N7: 元件1.D9, DFPlayer_Mini1.RX
  5V: 元件1.5V, 元件2.VCC
  N8: 元件1.A4, LED5.red_anode
  N9: 元件1.A1, LED5.blue_anode
  N10: 元件1.A0, LED5.green_anode
  N11: DFPlayer_Mini1.SPK1, SP1.-
  N12: DFPlayer_Mini1.GND#9, SP1.+
  N13: U1.pin2, Mod1.pin6
  N14: U2.GND, Mod1.pin2
  N15: U2.VBUS, Mod1.pin1
  N16: Mod1.pin3, U3.S
  N17: Mod1.pin4, BAT1.+, BAT3.+
  N18: BAT1.-, BAT3.-

custom parts:
  DFPlayer MINI: MP3 module by DFRobot.com for playing Music from an SD-Card. Supports WAV and MP3 files.
  LM2596-Step-Down-Converter: A dummy, proxy, ersatz, stand-in part for whatever you want. With 4 pins on a 100 mil inline pin header footprint.
  TP4056: TP4056 Lithium battery charger / protection module. (this one has the pins on .1 boundaried unlike the original)
  18650 battery holder: 18650 Battery Holder
